# Fritzing sketch RC-Sound_Modul (saved by Fritzing 0.9.3b)

parts:
  Bauteil1 = MicroSD Card Module
  Bauteil2 = Arduino Pro Mini (5V)
  Eingang = female pin header, 3 pins [form="♀ (female)"]
  Ausgang = female pin header, 3 pins [form="♀ (female)"]
  Diesel = female pin header, 3 pins [form="♀ (female)"]
  Sound1 = female pin header, 3 pins [form="♀ (female)"]
  Ton_out = female pin header, 3 pins [form="♀ (female)"]
  Sound2 = female pin header, 3 pins [form="♀ (female)"]
  R1 = Resistor [tolerance=±5% resistance=220 package=THT]
  C1 = Ceramic Capacitor [capacitance=100nF package="100 mil [THT, multilayer]"]

nets:
  GND: Bauteil1.GND, Bauteil2.GND, Eingang.pin1, Ausgang.pin1, Ton_out.pin2, C1.1
  VCC: Bauteil1.VCC, Bauteil2.VCC
  N1: Bauteil1.MISO, Bauteil2.MISO
  N2: Bauteil1.MOSI, Bauteil2.MOSI
  N3: Bauteil1.SCK, Bauteil2.SCK
  N4: Bauteil1.CS, Bauteil2.D10
  N5: Bauteil2.RAW, Eingang.pin2, Ausgang.pin2
  N6: Bauteil2.D9, R1.Pin_0
  N7: Bauteil2.D7, Sound2.pin1
  N8: Bauteil2.D6, Sound2.pin3
  N9: Bauteil2.D5, Sound1.pin1
  N10: Bauteil2.D4, Sound1.pin3
  N11: Bauteil2.D3, Diesel.pin1
  N12: Bauteil2.D2, Eingang.pin3, Ausgang.pin3
  N13: Ton_out.pin1, R1.Pin_1

notes:
  Drehzahl
  RC-Sound Modul
